# Fritzing sketch light_90 (saved by Fritzing 0.8.7b)
circuit board: 0.742803cm x 2.15879cm
breadboards: 1

parts:
  J1 = female pin header, 2 pins [form="♀ (female)"]
  J2 = female pin header, 2 pins [form="♀ (female)"]

nets:
  N1: J1.pin1, J2.pin1
  N2: J1.pin2, J2.pin2
