# Fritzing sketch diagram (saved by Fritzing 0.6.3b)
breadboards: 1

parts:
  Arduino1 = Arduino
  R1 = Resistor [tolerance=±5% resistance=220 package=THT]
  LED1 = LED - 5mm [color="Green (555nm)" package="5 mm [THT]"]
  R2 = Resistor [tolerance=±5% resistance=220 package=THT]
  LED2 = LED - 5mm [color="Red (633nm)" package="5 mm [THT]"]

nets:
  N1: Arduino1.GND, LED1.cathode, LED2.cathode
  N2: Arduino1.D10, R2.Pin_0
  N3: Arduino1.D9, R1.Pin_0
  N4: R1.Pin_1, LED1.anode
  N5: R2.Pin_1, LED2.anode
